// Digital circuit 74163_exam.dig as structural Verilog
// 74163 exam pin labels EP/ET/~R/~LD/D0-3/CLK/C/Q
module _74163_exam (
  input  nLD,
  input  nR,
  input  CLK,
  input  ET,
  input  EP,
  input  D0,
  input  D1,
  input  D2,
  input  D3,
  input  VCC,
  input  GND,
  output C,
  output Q0,
  output Q1,
  output Q2,
  output Q3
);

  wire add_1_c_o, and_1_out;
  wire [3:0] add_1_s, multiplexer_1_out, multiplexer_2_out, multiplexer_3_out;

  PowerSupply powersupply_1 (.VDD(VCC), .GND(GND));
  Add #(.Bits(4)) add_1 (.a({Q3, Q2, Q1, Q0}), .b(4'b0001), .c_i(1'b0), .s(add_1_s), .c_o(add_1_c_o));
  and and_1 (and_1_out, EP, ET);
  Multiplexer #(.Bits(4)) multiplexer_1 (
    .sel(and_1_out), .in_0({Q3, Q2, Q1, Q0}), .in_1(add_1_s), .out(multiplexer_1_out));
  Multiplexer #(.Bits(4)) multiplexer_2 (
    .sel(nLD), .in_0({D3, D2, D1, D0}), .in_1(multiplexer_1_out), .out(multiplexer_2_out));
  Multiplexer #(.Bits(4)) multiplexer_3 (.sel(nR), .in_0(4'b0000), .in_1(multiplexer_2_out), .out(multiplexer_3_out));
  and and_2 (C, add_1_c_o, ET);
  D_FF #(.Bits(4)) Q (.D(multiplexer_3_out), .C(CLK), .Q({Q3, Q2, Q1, Q0}));  // open: nQ

  // Notes on the sheet:
  //   nLD: pin 9
  //   nR: pin 1
  //   CLK: pin 2
  //   C: pin 15
  //   ET: pin 10
  //   EP: pin 7
  //   D0: pin 3
  //   D1: pin 4
  //   D2: pin 5
  //   D3: pin 6
  //   Q0: pin 14
  //   Q1: pin 13
  //   Q2: pin 12
  //   Q3: pin 11
  //   VCC: pin 16, default 1
  //   GND: pin 8
endmodule

/* Test case:
CP ~SR ~PE CET CEP   P3 P2 P1 P0 Q3 Q2 Q1 Q0

# load
loop(i,4)
loop(n,16)
C  1   0   bits(2,i) bits(4,n)   bits(4,n)
end loop
end loop

# reset
loop(i,8)
loop(n,16)
C  1   0   0   0     bits(4,n)   bits(4,n)
C  0   bits(3,i)     bits(4,n)   bits(4,0)
end loop
end loop

# count
loop(n,16)
C  1   1   1   1     bits(4,0)   bits(4,n+1)
end loop

# hold
loop(n,16)
C  1   0   0   0     bits(4,n)   bits(4,n)
C  1   1   0   0     bits(4,n)   bits(4,n)
C  1   1   1   0     bits(4,n)   bits(4,n)
C  1   1   0   1     bits(4,n)   bits(4,n)
end loop
*/
